# Fritzing sketch Multiblink (saved by Fritzing 0.9.8b)
circuit board: 8.46667cm x 5.64444cm
breadboards: 1

parts:
  Arduino_UNO = Arduino Uno (Rev3)
  LED1 = LED - 5mm [color="Yellow (592nm)" current=0.030 package="5 mm [THT]"]
  R1 = Resistor [tolerance=±5% resistance=220 power=0.25 package=THT]
  R2 = Resistor [tolerance=±5% power=0.25 resistance=220 package=THT]
  LED2 = LED - 5mm [color="Yellow (592nm)" current=0.030 package="5 mm [THT]"]
  R3 = Resistor [tolerance=±5% power=0.25 resistance=220 package=THT]
  LED3 = LED - 5mm [color="Yellow (592nm)" current=0.030 package="5 mm [THT]"]
  R4 = Resistor [tolerance=±5% power=0.25 resistance=220 package=THT]
  LED4 = LED - 5mm [color="Yellow (592nm)" current=0.030 package="5 mm [THT]"]
  R5 = Resistor [tolerance=±5% power=0.25 resistance=220 package=THT]
  LED5 = LED - 5mm [color="Yellow (592nm)" current=0.030 package="5 mm [THT]"]
  R6 = Resistor [tolerance=±5% power=0.25 resistance=220 package=THT]
  LED6 = LED - 5mm [color="Yellow (592nm)" current=0.030 package="5 mm [THT]"]

nets:
  N1: Arduino_UNO.D8, R6.Pin_0
  N2: Arduino_UNO.D9_PWM, R5.Pin_0
  N3: Arduino_UNO.D10_PWM/SS, R4.Pin_0
  N4: Arduino_UNO.D11_PWM/MOSI, R3.Pin_0
  N5: Arduino_UNO.D12/MISO, R2.Pin_0
  N6: Arduino_UNO.D13/SCK, R1.Pin_0
  N7: Arduino_UNO.GND, LED1.cathode, LED2.cathode, LED3.cathode, LED4.cathode, LED5.cathode, LED6.cathode
  N8: LED1.anode, R1.Pin_1
  N9: R2.Pin_1, LED2.anode
  N10: R3.Pin_1, LED3.anode
  N11: R4.Pin_1, LED4.anode
  N12: R5.Pin_1, LED5.anode
  N13: R6.Pin_1, LED6.anode

notes:
  Connected Objects and the IoT, Arduino basics - blinky-blinky - Hand-In, Ilja Tihhanovski, 1
