# Fritzing sketch RFB LED (saved by Fritzing 0.9.8b)
breadboards: 1

parts:
  LED1 = RGB LED (com. anode, rbg) [package="5 mm [THT]"]
  R1 = Resistor [tolerance=±5% resistance=220 package="1206 [SMD]"]
  R2 = Resistor [tolerance=±5% resistance=220 package="1206 [SMD]"]
  R3 = Resistor [tolerance=±5% resistance=220 package="1206 [SMD]"]
  MC1 = Arduino Uno (Rev3)

nets:
  N1: LED1.red_cathode, R1.Pin_0
  N2: LED1.common_anode, MC1.5V
  N3: LED1.blue_cathode, R2.Pin_0
  N4: LED1.green_cathode, R3.Pin_0
  N5: R1.Pin_1, MC1.D3_PWM
  N6: R2.Pin_1, MC1.D5_PWM
  N7: R3.Pin_1, MC1.D6_PWM

notes:
  Connected Objects and the IoT, LED Disco Light - Pulse-Width Modulation, Ilja Tihhanovski, 1
