# Fritzing sketch Buttons (saved by Fritzing 0.9.8b)
breadboards: 1

parts:
  Controller = Arduino Uno (Rev3)
  R1 = Resistor [tolerance=±5% resistance=220 package="2512 [SMD]"]
  LED1 = smd LED [color="Red (633nm)" package="1206 [SMD]"]
  Button_B = Momentary Switch [package=ksa_sealed_tac_switch]
  Button_A = Momentary Switch [package=ksa_sealed_tac_switch]

nets:
  N1: Controller.D8, Button_B.1
  N2: Controller.D9_PWM, Button_A.1
  N3: Controller.GND, LED1.cathode, Button_B.3, Button_A.3
  N4: Controller.D5_PWM, R1.Pin_0
  N5: R1.Pin_1, LED1.anode

notes:
  Connected Objects and the IoT, Buttons up, Ilja Tihhanovski, 1
