# Fritzing sketch What Goes Up Must Come Down (saved by Fritzing 0.9.8b)
breadboards: 1

parts:
  R3 = Resistor [tolerance=±5% resistance=220 package="1206 [SMD]"]
  R2 = Resistor [tolerance=±5% resistance=220 package="1206 [SMD]"]
  R1 = Resistor [tolerance=±5% resistance=220 package="1206 [SMD]"]
  LED1 = RGB LED (com. anode, rbg) [package="5 mm [THT]"]
  Controller = Arduino Uno (Rev3)
  Button_R = Momentary Switch [package=ksa_sealed_tac_switch]
  Button_G = Momentary Switch [package=ksa_sealed_tac_switch]
  Button_B = Momentary Switch [package=ksa_sealed_tac_switch]
  Button_OFF = Momentary Switch [package=ksa_sealed_tac_switch]

nets:
  N1: R3.Pin_0, Controller.D11_PWM/MOSI
  N2: R3.Pin_1, LED1.red_cathode
  N3: R2.Pin_0, Controller.D10_PWM/SS
  N4: R2.Pin_1, LED1.blue_cathode
  N5: R1.Pin_0, Controller.D9_PWM
  N6: R1.Pin_1, LED1.green_cathode
  N7: LED1.common_anode, Controller.5V
  N8: Controller.D4, Button_OFF.3
  N9: Controller.D5_PWM, Button_B.3
  N10: Controller.D6_PWM, Button_G.3
  N11: Controller.D7, Button_R.3
  N12: Controller.GND, Button_R.1, Button_G.1, Button_B.1, Button_OFF.1

notes:
  Connected Objects and the IoT, What Goes Up, Must Come Down...
  , Ilja Tihhanovski, 1
