# Fritzing sketch Analog input 2 (saved by Fritzing 0.9.8b)
breadboards: 1

parts:
  LED1 = smd LED [color="Red (633nm)" package="0603 [SMD]"]
  LED2 = smd LED [color="Blue (525nm)" package="0603 [SMD]"]
  LED3 = smd LED [color="Green (560nm)" package="0603 [SMD]"]
  R1 = Resistor [tolerance=±5% resistance=220 package="2010 [SMD]"]
  R2 = Resistor [tolerance=±5% resistance=220 package="2010 [SMD]"]
  MC = Arduino Uno (Rev3) - ICSP
  R3 = Resistor [tolerance=±5% resistance=220 package="2010 [SMD]"]
  R4 = Resistor [tolerance=±5% resistance=1k package="2010 [SMD]"]
  R5 = PHOTOCELL [package=photocell]
  S1 = Momentary Switch [package=ksa_sealed_tac_switch]
  S2 = Momentary Switch [package=ksa_sealed_tac_switch]
  R6 = Resistor [tolerance=±5% resistance=1k package="2010 [SMD]"]
  R7 = Resistor [tolerance=±5% resistance=1k package="2010 [SMD]"]

nets:
  N1: LED1.cathode, LED2.cathode, LED3.cathode, MC.GND, R4.Pin_0, S2.1
  N2: LED1.anode, R1.Pin_0
  N3: LED2.anode, R2.Pin_0
  N4: LED3.anode, R3.Pin_0
  N5: R1.Pin_1, MC.D13/SCK
  N6: R2.Pin_1, MC.D12/MISO
  N7: MC.A0, R4.Pin_1, R5.P$1
  N8: MC.A1, R6.Pin_1, R7.Pin_0
  N9: MC.D11_PWM/MOSI, R3.Pin_1
  N10: MC.5V, R5.P$2, S1.3
  N11: S1.1, R7.Pin_1
  N12: S2.3, R6.Pin_0

notes:
  Connected Objects and the IoT, Analog input Ilja Tihhanovski, 1
