# Fritzing sketch Proximity alert (saved by Fritzing 0.9.8b)
breadboards: 1

parts:
  S1 = SWITCH-MOMENTARY-2 [package=tactile-pth-12mm]
  MC = Arduino Uno (Rev3) - ICSP
  LED1 = smd LED [color="Yellow (595nm)" package="0603 [SMD]"]
  R1 = Resistor [tolerance=±5% resistance=220 package="2010 [SMD]"]
  HC-SR04 = HC-SR04 Ultrasonic Distance Sensor
  Buzzer = Piezo Speaker
  LED2 = smd LED [color="Yellow (595nm)" package="0603 [SMD]"]
  R2 = Resistor [tolerance=±5% resistance=220 package="2010 [SMD]"]
  LED3 = smd LED [color="Yellow (595nm)" package="0603 [SMD]"]
  R3 = Resistor [tolerance=±5% resistance=220 package="2010 [SMD]"]
  LED4 = smd LED [color="Yellow (595nm)" package="0603 [SMD]"]
  R4 = Resistor [tolerance=±5% resistance=220 package="2010 [SMD]"]
  LED5 = smd LED [color="Yellow (595nm)" package="0603 [SMD]"]
  R5 = Resistor [tolerance=±5% resistance=220 package="2010 [SMD]"]

nets:
  N1: S1.1, MC.D10_PWM/SS
  GND: S1.2, MC.GND, LED1.cathode, HC-SR04.GND, Buzzer.pin2, LED2.cathode, LED3.cathode, LED4.cathode, LED5.cathode
  5V: MC.5V, HC-SR04.VCC
  N2: MC.D8, Buzzer.pin1
  N3: MC.D9_PWM, R1.Pin_0
  N4: MC.D11_PWM/MOSI, HC-SR04.ECHO
  N5: MC.D12/MISO, HC-SR04.TRIG
  N6: MC.D4, R5.Pin_0
  N7: MC.D5_PWM, R4.Pin_0
  N8: MC.D6_PWM, R3.Pin_0
  N9: MC.D7, R2.Pin_0
  N10: LED1.anode, R1.Pin_1
  N11: LED2.anode, R2.Pin_1
  N12: LED3.anode, R3.Pin_1
  N13: LED4.anode, R4.Pin_1
  N14: LED5.anode, R5.Pin_1

notes:
  Arduino basics - Proximity alert, Ilja Tihhanovski
