# Fritzing sketch Rotary encoder (saved by Fritzing 0.9.8b)
breadboards: 1

parts:
  LED1 = RGB LED (com. anode, rbg) [package="5 mm [THT]"]
  R1 = Resistor [tolerance=±5% resistance=220 package="1206 [SMD]"]
  R2 = Resistor [tolerance=±5% resistance=220 package="1206 [SMD]"]
  R3 = Resistor [tolerance=±5% resistance=220 package="1206 [SMD]"]
  MC1 = Arduino Uno (Rev3)
  RE1 = KY-040 Rotary encoder [package="Breakout board"]
  S1 = SWITCH-MOMENTARY-2 [package=tactile_switch_smd-2]
  S2 = SWITCH-MOMENTARY-2 [package=tactile_switch_smd-2]
  S3 = SWITCH-MOMENTARY-2 [package=tactile_switch_smd-2]
  S4 = SWITCH-MOMENTARY-2 [package=tactile_switch_smd-2]

nets:
  N1: LED1.red_cathode, R1.Pin_0
  5V: LED1.common_anode, MC1.5V, RE1.Vcc
  N2: LED1.blue_cathode, R2.Pin_0
  N3: LED1.green_cathode, R3.Pin_0
  N4: R1.Pin_1, MC1.D3_PWM
  N5: R2.Pin_1, MC1.D5_PWM
  N6: R3.Pin_1, MC1.D6_PWM
  N7: MC1.D8, RE1.CLK
  N8: MC1.D9_PWM, S1.1
  N9: MC1.D10_PWM/SS, S2.1
  N10: MC1.D11_PWM/MOSI, S3.1
  N11: MC1.D12/MISO, S4.1
  N12: MC1.D4, RE1.SW
  N13: MC1.D7, RE1.DT
  GND: MC1.GND, RE1.GND, S1.2, S2.2, S3.2, S4.2

notes:
  Connected Objects and the IoT, Rotary Light Controller, Ilja Tihhanovski, 1
  Rotary encoder KY-040 scheme by flaix
  from: https://forum.fritzing.org/t/ky-040-rotary-encoder-breakout-board-part/11073/10

custom parts:
  KY-040 Rotary encoder: KY-040 Rotary Encoder with switch on breakout borad from AZ Delivery
