# Fritzing sketch I2C (saved by Fritzing 0.9.8b)
breadboards: 1

parts:
  Slave_1 = Arduino Uno (Rev3)
  Master = Arduino Pro Micro (Clone) 05
  LED1 = LED - 5mm [color="Red (633nm)" current=0.030 package="5 mm [THT]"]
  R1 = Resistor [tolerance=±5% resistance=220 package="1206 [SMD]"]
  LED2 = LED - 5mm [color="Red (633nm)" current=0.030 package="5 mm [THT]"]
  R2 = Resistor [tolerance=±5% resistance=220 package="1206 [SMD]"]
  LED3 = LED - 5mm [color="Red (633nm)" current=0.030 package="5 mm [THT]"]
  R3 = Resistor [tolerance=±5% resistance=220 package="1206 [SMD]"]
  S1 = SWITCH-MOMENTARY-2 [package=tactile_switch_smd-2]
  Slave_2 = Arduino Uno (Rev3)
  LED4 = LED - 5mm [color="Red (633nm)" current=0.030 package="5 mm [THT]"]
  LED5 = LED - 5mm [color="Red (633nm)" current=0.030 package="5 mm [THT]"]
  LED6 = LED - 5mm [color="Red (633nm)" current=0.030 package="5 mm [THT]"]
  R4 = Resistor [tolerance=±5% resistance=220 package="1206 [SMD]"]
  R5 = Resistor [tolerance=±5% resistance=220 package="1206 [SMD]"]
  R6 = Resistor [tolerance=±5% resistance=220 package="1206 [SMD]"]
  S2 = SWITCH-MOMENTARY-2 [package=tactile_switch_smd-2]

nets:
  N1: Slave_1.A4/SDA, Master.connector18, Slave_2.A4/SDA
  N2: Slave_1.A5/SCL, Master.connector19, Slave_2.A5/SCL
  N3: Slave_1.D3_PWM, R1.Pin_1
  N4: Slave_1.D4, R2.Pin_1
  N5: Slave_1.D5_PWM, R3.Pin_1
  N6: Slave_1.D6_PWM, S1.1
  GND: Slave_1.GND, Master.connector16, LED1.cathode, LED2.cathode, LED3.cathode, S1.2, Slave_2.GND, LED4.cathode, LED5.cathode, LED6.cathode, S2.2
  N7: LED1.anode, R1.Pin_0
  N8: LED2.anode, R2.Pin_0
  N9: LED3.anode, R3.Pin_0
  N10: Slave_2.D3_PWM, R6.Pin_1
  N11: Slave_2.D4, R4.Pin_1
  N12: Slave_2.D5_PWM, R5.Pin_1
  N13: Slave_2.D6_PWM, S2.1
  N14: LED4.anode, R6.Pin_0
  N15: LED5.anode, R5.Pin_0
  N16: LED6.anode, R4.Pin_0

notes:
  Connected Objects and the IoT, Traffic lights with I2C, Ilja Tihhanovski, 1
