# Fritzing sketch NoLoops (saved by Fritzing 0.9.8b)
breadboards: 1

parts:
  MC = Arduino Uno (Rev3)
  LED1 = LED - 5mm [color="Red (633nm)" current=30mA package="5 mm [THT]"]
  R1 = Resistor [tolerance=±5% resistance=220 package="1206 [SMD]"]
  LED2 = LED - 5mm [color="Yellow (595nm)" current=30mA package="5 mm [THT]"]
  R2 = Resistor [tolerance=±5% resistance=220 package="1206 [SMD]"]
  LED3 = LED - 5mm [color="Green (565nm)" current=30mA package="5 mm [THT]"]
  R3 = Resistor [tolerance=±5% resistance=220 package="1206 [SMD]"]
  LED4 = LED - 5mm [color="Blue (525nm)" current=30mA package="5 mm [THT]"]
  R4 = Resistor [tolerance=±5% resistance=220 package="1206 [SMD]"]
  S1 = SWITCH-MOMENTARY-2 [package=tactile_switch_smd-2]
  S3 = SWITCH-MOMENTARY-2 [package=tactile_switch_smd-2]
  S4 = SWITCH-MOMENTARY-2 [package=tactile_switch_smd-2]
  S2 = SWITCH-MOMENTARY-2 [package=tactile_switch_smd-2]
  D2 = Diode [package=diode-1n4148]
  D1 = Diode [package=diode-1n4148]
  D3 = Diode [package=diode-1n4148]
  C1 = Capacitor Polarized [part_number="10 µF" package=panasonic_h13]

nets:
  N1: MC.D8, S1.1, D1.C
  N2: MC.D9_PWM, S2.1, D2.C
  N3: MC.D10_PWM/SS, S3.1, D3.C
  N4: MC.GND, LED1.cathode, LED2.cathode, LED3.cathode, LED4.cathode, S1.2, S3.2, S4.2, S2.2, C1.-
  N5: MC.D2, S4.1, D2.A, D1.A, D3.A, C1.+
  N6: MC.D3_PWM, R1.Pin_1
  N7: MC.D4, R2.Pin_1
  N8: MC.D5_PWM, R3.Pin_1
  N9: MC.D6_PWM, R4.Pin_1
  N10: LED1.anode, R1.Pin_0
  N11: LED2.anode, R2.Pin_0
  N12: LED3.anode, R3.Pin_0
  N13: LED4.anode, R4.Pin_0

notes:
  Connected Objects and the IoT, No Loops, Ilja Tihhanovski, 1
