# Fritzing sketch Interrupt Lightswitch (saved by Fritzing 0.9.8b)
breadboards: 1

parts:
  MC = Arduino Uno (Rev3) - ICSP
  LED1 = LED - 5mm [color="Red (633nm)" current=0.030 package="5 mm [THT]"]
  R1 = Resistor [tolerance=±5% resistance=220 package="1206 [SMD]"]
  S1 = SWITCH-MOMENTARY-2 [package=tactile_switch_smd-2]
  S2 = SWITCH-MOMENTARY-2 [package=tactile_switch_smd-2]
  AM1 = Multimeter (AC Current)
  V1 = DC Power [voltage=5V]

nets:
  N1: MC.D13/SCK, R1.Pin_1
  N2: MC.D2, S1.1
  N3: MC.D3_PWM, S2.1
  N4: MC.GND, LED1.cathode, S1.2, S2.2, V1.V-
  N5: MC.VIN, AM1.COM_Probe
  N6: LED1.anode, R1.Pin_0
  N7: AM1.A_Probe, V1.V+

notes:
  Connected Objects and the IoT, Interrupt Lightswitch Ilja Tihhanovski
