# Fritzing sketch DutyCycling2 (saved by Fritzing 0.9.8b)
breadboards: 1

parts:
  MC = Arduino Uno (Rev3) - ICSP
  LED1 = LED - 5mm [color="Red (660nm)" current=30mA package="5 mm [THT]"]
  R1 = Resistor [tolerance=±5% resistance=220 package="1206 [SMD]"]
  S1 = SWITCH-MOMENTARY-2 [package=tactile_switch_smd-2]
  C1 = Capacitor Polarized [part_number="10 µF" package=panasonic_h13]

nets:
  N1: MC.ICSP_MISO, MC.D12/MISO, LED1.anode
  N2: MC.GND, R1.Pin_0, S1.2, C1.-
  N3: MC.D2, S1.1, C1.+
  N4: LED1.cathode, R1.Pin_1

notes:
  Connected Objects and the IoT, Watchdog based duty-cycling 1, Ilja Tihhanovski
