# Fritzing sketch DeepsleepEsp8266 (saved by Fritzing 0.9.8b)
breadboards: 1

parts:
  MC = ESP8266 WiFi Module [part_number=ESP8266]
  R1 = Resistor [tolerance=±5% resistance=1k package="1206 [SMD]"]
  LED1 = LED - 5mm [color="Red (633nm)" current=0.030 package="5 mm [THT]"]
  R2 = Resistor [tolerance=±5% resistance=220 package="1206 [SMD]"]

nets:
  N1: MC.D0, R1.Pin_0
  N2: MC.D1, LED1.anode
  N3: MC.GND, R2.Pin_1
  N4: MC.RST, R1.Pin_1
  N5: LED1.cathode, R2.Pin_0

notes:
  Connected Objects and the IoT, Duty-cycling and deep sleep in ESP8266, Ilja Tihhanovski
