# Fritzing sketch BLE (saved by Fritzing 0.9.8b)
breadboards: 1

parts:
  MC1 = Arduino Uno (Rev3) - ICSP
  LCD = IC, SIP package, 4 pins [chip_label=1602A]
  BLE = IC, SIP package, 6 pins [chip_label=BLE]
  R1 = Resistor [tolerance=±5% resistance=1k package="1206 [SMD]"]
  R2 = Resistor [tolerance=±5% resistance=2k package="1206 [SMD]"]
  LED2 = LED - 5mm [color="Red (660nm)" current=30mA package="5 mm [THT]"]
  R3 = Resistor [tolerance=±5% resistance=220 package="1206 [SMD]"]
  LED3 = LED - 5mm [color="Red (660nm)" current=30mA package="5 mm [THT]"]
  R4 = Resistor [tolerance=±5% resistance=220 package="1206 [SMD]"]
  LED4 = LED - 5mm [color="Red (660nm)" current=30mA package="5 mm [THT]"]
  R5 = Resistor [tolerance=±5% resistance=220 package="1206 [SMD]"]

nets:
  N1: MC1.A4/SDA, LCD.pin2
  N2: MC1.A5/SCL, LCD.pin1
  N3: MC1.5V, BLE.pin2
  GND: MC1.GND, LCD.pin4, BLE.pin3, R1.Pin_0, R3.Pin_0, R4.Pin_0, R5.Pin_0
  N4: MC1.D8, BLE.pin6
  N5: MC1.D9_PWM, R2.Pin_1
  N6: MC1.D10_PWM/SS, BLE.pin4
  N7: MC1.D2, LED2.anode
  N8: MC1.D3_PWM, LED3.anode
  N9: MC1.D4, LED4.anode
  N10: MC1.VIN, LCD.pin3
  N11: BLE.pin5, R1.Pin_1, R2.Pin_0
  N12: LED2.cathode, R3.Pin_1
  N13: LED3.cathode, R4.Pin_1
  N14: LED4.cathode, R5.Pin_1

notes:
  Connected Objects and the IoT, I've Got A Light Case of the Blue(tooth)s, Ilja Tihhanovski
