# Fritzing sketch Mosquittoes (saved by Fritzing 0.9.8b)
breadboards: 1

parts:
  MC2 = Arduino Uno (Rev3) - ICSP
  DHT11 = IC, SIP package, 3 pins [chip_label=DHT11]

nets:
  N1: MC2.5V, DHT11.pin1
  N2: MC2.GND, DHT11.pin3
  N3: MC2.D2, DHT11.pin2

notes:
  Connected Objects and the IoT, MQTT: Trapping mosquitoes, Ilja Tihhanovski
