# Fritzing sketch MQTT_PubSubClient (saved by Fritzing 0.9.8b)
breadboards: 1

parts:
  DHT11 = IC, SIP package, 3 pins [chip_label=DHT11]
  MC = Heltec WiFi LoRa 32 V2 [part_number="ESP32 DevKit"]

nets:
  N1: DHT11.pin1, MC.pin_16, MC.pin_17
  N2: DHT11.pin2, MC.pin_34
  N3: DHT11.pin3, MC.GND

notes:
  Connected Objects and the IoT, PubSubClient and ESP8266, Ilja Tihhanovski
  Internal LED is used to blink
