# Fritzing sketch VLC circuit (saved by Fritzing 0.9.8b)
breadboards: 1

parts:
  Sender = Arduino Micro (Rev3)
  Receiver = Arduino Uno (Rev3) - ICSP
  LED1 = LED - 5mm [color="Blue (525nm)" current=0.030 package="5 mm [THT]"]
  R1 = Resistor [tolerance=±5% resistance=220 package="1206 [SMD]"]
  S1 = SWITCH-MOMENTARY-2 [package=tactile_switch_smd-2]
  LDR1 = Photocell (LDR) [package=THT]
  R3 = Resistor [tolerance=±5% resistance=1k package="1206 [SMD]"]

nets:
  N1: Sender.GND, R1.Pin_1, S1.2
  N2: Sender.D6_PWM/A7, S1.1
  N3: Sender.D7, LED1.anode
  N4: Receiver.5V, LDR1.pin_1
  N5: Receiver.GND, R3.Pin_0
  N6: Receiver.D2, LDR1.pin_0, R3.Pin_1
  N7: LED1.cathode, R1.Pin_0

notes:
  Connected Objects and the IoT, Visible light communications, Ilja Tihhanovski
